// Digital circuit lab2_part3.dig as structural Verilog
module lab2_part3 (
  input  clk,
  input  in0,
  input  in1,
  input  in2,
  input  in3,
  input  sel_write_1,
  input  sel_write_0,
  input  sel_readA_1,
  input  sel_readA_0,
  input  sel_readB_1,
  input  sel_readB_0,
  output out0,
  output out1,
  output out2,
  output out3,
  output reg0_0,
  output reg0_1,
  output reg0_2,
  output reg0_3,
  output reg1_0,
  output reg1_1,
  output reg1_2,
  output reg1_3,
  output reg2_0,
  output reg2_1,
  output reg2_2,
  output reg2_3,
  output reg3_0,
  output reg3_1,
  output reg3_2,
  output reg3_3,
  output inA_0,
  output inA_1,
  output inA_2,
  output inA_3,
  output inB_0,
  output inB_1,
  output inB_2,
  output inB_3
);

  wire and_1_out, and_2_out, and_3_out, and_4_out, decoder_1_out_0, decoder_1_out_1, decoder_1_out_2,
       decoder_1_out_3;

  Decoder #(.Selector_Bits(2)) decoder_1 (
    .sel({sel_write_1, sel_write_0}), .out_0(decoder_1_out_0), .out_1(decoder_1_out_1),
    .out_2(decoder_1_out_2), .out_3(decoder_1_out_3));
  and and_1 (and_1_out, decoder_1_out_0, 1'b1);
  Register #(.Bits(4)) register_1 (
    .D({in3, in2, in1, in0}), .C(clk), .en(and_1_out), .Q({reg0_3, reg0_2, reg0_1, reg0_0}));
  and and_2 (and_2_out, decoder_1_out_1, 1'b1);
  Register #(.Bits(4)) register_2 (
    .D({in3, in2, in1, in0}), .C(clk), .en(and_2_out), .Q({reg1_3, reg1_2, reg1_1, reg1_0}));
  and and_3 (and_3_out, decoder_1_out_2, 1'b1);
  Register #(.Bits(4)) register_3 (
    .D({in3, in2, in1, in0}), .C(clk), .en(and_3_out), .Q({reg2_3, reg2_2, reg2_1, reg2_0}));
  and and_4 (and_4_out, decoder_1_out_3, 1'b1);
  Register #(.Bits(4)) register_4 (
    .D({in3, in2, in1, in0}), .C(clk), .en(and_4_out), .Q({reg3_3, reg3_2, reg3_1, reg3_0}));
  Multiplexer #(.Selector_Bits(2), .Bits(4)) multiplexer_1 (
    .sel({sel_readA_1, sel_readA_0}), .in_0({reg0_3, reg0_2, reg0_1, reg0_0}),
    .in_1({reg1_3, reg1_2, reg1_1, reg1_0}), .in_2({reg2_3, reg2_2, reg2_1, reg2_0}),
    .in_3({reg3_3, reg3_2, reg3_1, reg3_0}), .out({inA_3, inA_2, inA_1, inA_0}));
  Multiplexer #(.Selector_Bits(2), .Bits(4)) multiplexer_2 (
    .sel({sel_readB_1, sel_readB_0}), .in_0({reg0_3, reg0_2, reg0_1, reg0_0}),
    .in_1({reg1_3, reg1_2, reg1_1, reg1_0}), .in_2({reg2_3, reg2_2, reg2_1, reg2_0}),
    .in_3({reg3_3, reg3_2, reg3_1, reg3_0}), .out({inB_3, inB_2, inB_1, inB_0}));
  lab2_part1 lab2_part1_1 (
    .inA_0(inA_0), .inA_1(inA_1), .inA_2(inA_2), .inA_3(inA_3), .inB_0(inB_0), .inB_1(inB_1), .inB_2(inB_2),
    .inB_3(inB_3), .out0(out0), .out1(out1), .out2(out2), .out3(out3));
  Seven_Seg_Hex seven_seg_hex_1 (.d({inA_3, inA_2, inA_1, inA_0}), .dp(1'b0));
  Seven_Seg_Hex seven_seg_hex_2 (.d({reg3_3, reg3_2, reg3_1, reg3_0}), .dp(1'b0));
  Seven_Seg_Hex seven_seg_hex_3 (.d({in3, in2, in1, in0}), .dp(1'b0));
  Seven_Seg_Hex seven_seg_hex_4 (.d({inB_3, inB_2, inB_1, inB_0}), .dp(1'b0));
  Seven_Seg_Hex seven_seg_hex_5 (.d({reg2_3, reg2_2, reg2_1, reg2_0}), .dp(1'b0));
  Seven_Seg_Hex seven_seg_hex_6 (.d({2'b00, sel_write_1, sel_write_0}), .dp(1'b0));
  Seven_Seg_Hex seven_seg_hex_7 (.d({2'b00, sel_readA_1, sel_readA_0}), .dp(1'b0));
  Seven_Seg_Hex seven_seg_hex_8 (.d({out3, out2, out1, out0}), .dp(1'b0));
  Seven_Seg_Hex seven_seg_hex_9 (.d({reg1_3, reg1_2, reg1_1, reg1_0}), .dp(1'b0));
  Seven_Seg_Hex seven_seg_hex_10 (.d({2'b00, sel_readB_1, sel_readB_0}), .dp(1'b0));
  Seven_Seg_Hex seven_seg_hex_11 (.d({reg0_3, reg0_2, reg0_1, reg0_0}), .dp(1'b0));

  // Notes on the sheet:
  //   Interface (do not edit the content inside this box)
  //   Inputs
  //   Keypad
  //   Outputs
  //   Registers
  //   Values read into ALU inputs
  //   Rotatee
  //   Register 3
  //   Synchronizing Clock
  //   Rotation amount:
  //   Register Selection: Write-to
  //   Register 2
  //   Register Selection: Read-from
  //   ALU Output
  //   ALU input A register address:
  //   Register 1
  //   ALU input B register address:
  //   Register 0
endmodule

/* Test case:
clk in3 in2 in1 in0 sel^write_1 sel^write_0 sel^readA_1 sel^readA_0 sel^readB_1 sel^readB_0  reg3_3 reg3_2 reg3_1 reg3_0 reg2_3 reg2_2 reg2_1 reg2_0 reg1_3 reg1_2 reg1_1 reg1_0 reg0_3 reg0_2 reg0_1 reg0_0 out3 out2 out1 out0
 0   0   0   0   0   0           0           0           0           0           0            0      0      0      0      0      0      0      0      0      0      0      0      0      0      0      0      0    0    0    0
 1   0   0   0   0   0           0           0           0           0           0            0      0      0      0      0      0      0      0      0      0      0      0      0      0      0      0      0    0    0    0
 0   0   1   0   1   1           1           0           0           0           0            0      0      0      0      0      0      0      0      0      0      0      0      0      0      0      0      0    0    0    0
 1   0   1   0   1   1           1           0           0           0           0            0      1      0      1      0      0      0      0      0      0      0      0      0      0      0      0      0    0    0    0
 0   0   0   0   1   0           1           0           0           0           0            0      1      0      1      0      0      0      0      0      0      0      0      0      0      0      0      0    0    0    0
 1   0   0   0   1   0           1           0           0           0           0            0      1      0      1      0      0      0      0      0      0      0      1      0      0      0      0      0    0    0    0
 0   0   0   0   0   0           0           1           1           0           1            0      1      0      1      0      0      0      0      0      0      0      1      0      0      0      0      1    0    1    0
 1   0   0   0   0   0           0           1           1           0           1            0      1      0      1      0      0      0      0      0      0      0      1      0      0      0      0      1    0    1    0
 0   0   0   0   0   0           0           0           1           1           1            0      1      0      1      0      0      0      0      0      0      0      1      0      0      0      0      0    0    1    0
 1   0   0   0   0   0           0           0           1           1           1            0      1      0      1      0      0      0      0      0      0      0      1      0      0      0      0      0    0    1    0
*/
